# Fritzing sketch Task5.1p (saved by Fritzing 1.0.2b)
breadboards: 1

parts:
  Mod1 = Raspberry Pi 4B  # not connected
  LED1 = LED - 5mm [color="Red (633nm)" current=0.030A package="5 mm [THT]"]
  LED2 = LED - 5mm [color="Green (555nm)" current=0.030A package="5 mm [THT]"]
  LED3 = LED - 5mm [color="Blue (430nm)" current=0.030A package="5 mm [THT]"]
  Part1 = Adafruit T-Cobbler Plus [part_number="Adafruit #1989 and #2028"]
  R1 = Resistor [tolerance=±5% power=0.25W resistance=1k package=THT]
  R2 = Resistor [tolerance=±5% power=0.25W resistance=1k package=THT]
  R3 = Resistor [tolerance=±5% power=0.25W resistance=1k package=THT]

nets:
  N1: LED1.cathode, Part1.GPIO5
  N2: LED1.anode, R1.Pin_0
  N3: LED2.cathode, Part1.GPIO6
  N4: LED2.anode, R2.Pin_0
  N5: LED3.cathode, Part1.GPIO26
  N6: LED3.anode, R3.Pin_0
  N7: Part1.GND, R1.Pin_1, R2.Pin_1, R3.Pin_1

custom parts:
  Adafruit T-Cobbler Plus: The Raspberry Pi has landed on the Maker World like a 40-GPIO pinned, quad-USB ported, credit card sized bomb of DIY joy. And while you can use most of our great Model B accessories by hooking up our downgrade cable, its probably a good time to upgrade your set up and accessorize using all of the 40 pins. That's why we now carry the Assembled Adafruit Pi T-Cobbler Plus - Breakout + Cable for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
